# Fritzing sketch best_ticker_ever (saved by Fritzing 0.9.0b)
breadboards: 1

parts:
  CHARGER1 = USB_LiIon_LiPoly_Charger_v1.2
  Part1 = Spark Core (v1.0)
  NEOPIXEL1 = Neopixel 8x8 Matrix
  NEOPIXEL2 = Neopixel 8x8 Matrix
  NEOPIXEL3 = Neopixel 8x8 Matrix
  NEOPIXEL4 = Neopixel 8x8 Matrix
  JP1 = Header 2 [package=jst-2-pth]
  JP1_2 = Header 2 [package=jst-2-smd]
  SN74HCT245 = IC, DIP package, 20 pins [chip_label=SN74HCT245 part_number=296-1612-5-ND]
  R1 = Resistor [tolerance=±5% resistance=330 package=THT]

nets:
  N1: CHARGER1.load_minus_1, JP1.1, JP1_2.1
  N2: Part1.GND, NEOPIXEL1.GND#3
  N3: Part1.VIN, NEOPIXEL1.VCC#2, JP1.2
  N4: NEOPIXEL1.DIN, SN74HCT245.pin18, R1.Pin_0, R1.Pin_1
  N5: NEOPIXEL1.DOUT, NEOPIXEL2.DIN
  N6: NEOPIXEL1.VCC#5, NEOPIXEL2.VCC#2
  N7: NEOPIXEL1.GND#6, NEOPIXEL2.GND#3
  N8: NEOPIXEL2.DOUT, NEOPIXEL3.DIN
  N9: NEOPIXEL2.VCC#5, NEOPIXEL3.VCC#2
  N10: NEOPIXEL2.GND#6, NEOPIXEL3.GND#3
  N11: NEOPIXEL3.DOUT, NEOPIXEL4.DIN
  N12: NEOPIXEL3.VCC#5, NEOPIXEL4.VCC
  N13: NEOPIXEL3.GND#6, NEOPIXEL4.GND

custom parts:
  Neopixel 8x8 Matrix: Adafruit Neopixel 8x8 Matrix
